# Fritzing sketch wayAhead (saved by Fritzing 0.9.6b)

parts:
  Part1 = Arduino Nano (Rev3.0)
  S2 = Pushbutton [package="[SMD]"]
  microSD1 = MicroSD Card Module
  S1 = Pushbutton [package="[THT]"]
  GY-NEO6MV3 = SUP500F [package=sup500f]
  OLED_I2C1 = OLED 128x64 I2C Monochrome Display

nets:
  GND: Part1.GND, S2.Pin_1, S2.Pin_2, microSD1.GND, S1.Pin_1, S1.Pin_2, GY-NEO6MV3.GND, OLED_I2C1.GND
  N1: Part1.D3, GY-NEO6MV3.RX-I
  N2: Part1.D4, GY-NEO6MV3.TX-O
  N3: Part1.D5, S1.Pin_4
  N4: Part1.D6, S2.Pin_3, S2.Pin_4
  N5: Part1.D7, microSD1.CS
  N6: Part1.D11/MOSI, microSD1.MOSI
  N7: Part1.D12/MISO, microSD1.MISO
  5V: Part1.5V, GY-NEO6MV3.VCC
  N8: Part1.A5, OLED_I2C1.SCK
  N9: Part1.A4, OLED_I2C1.SDA
  3V3: Part1.3V3, microSD1.VCC, OLED_I2C1.VDD
  N10: Part1.D13/SCK, microSD1.SCK
